// Logisim project adder.circ as structural Verilog: 2 circuits, main circuit main
module main (
  input  [15:0] B,
  input  [15:0] A,
  input  sub,
  output [15:0] result,
  output ovf
);

  wire bitadder_1_cout, bitadder_2_cout, bitadder_3_cout, bitadder_4_cout, bitadder_5_cout, bitadder_6_cout,
       bitadder_7_cout, bitadder_8_cout, bitadder_9_cout, bitadder_10_cout, bitadder_11_cout,
       bitadder_12_cout, bitadder_13_cout, bitadder_14_cout, bitadder_15_cout, bitadder_16_cout, xor_2_out,
       xor_3_out, xor_4_out, xor_5_out, xor_6_out, xor_7_out, xor_8_out, xor_9_out, xor_10_out, xor_11_out,
       xor_12_out, xor_13_out, xor_14_out, xor_15_out, xor_16_out, xor_17_out;

  xor xor_1 (ovf, bitadder_1_cout, bitadder_2_cout);
  BitAdder bitadder_1 (.A(xor_2_out), .B(A[15]), .Cin(bitadder_2_cout), .Cout(bitadder_1_cout), .Sum(result[15]));
  xor xor_2 (xor_2_out, sub, B[15]);
  BitAdder bitadder_2 (.A(xor_3_out), .B(A[14]), .Cin(bitadder_3_cout), .Cout(bitadder_2_cout), .Sum(result[14]));
  xor xor_3 (xor_3_out, sub, B[14]);
  BitAdder bitadder_3 (.A(xor_4_out), .B(A[13]), .Cin(bitadder_4_cout), .Cout(bitadder_3_cout), .Sum(result[13]));
  xor xor_4 (xor_4_out, sub, B[13]);
  BitAdder bitadder_4 (.A(xor_5_out), .B(A[12]), .Cin(bitadder_5_cout), .Cout(bitadder_4_cout), .Sum(result[12]));
  xor xor_5 (xor_5_out, sub, B[12]);
  BitAdder bitadder_5 (.A(xor_7_out), .B(A[11]), .Cin(bitadder_7_cout), .Cout(bitadder_5_cout), .Sum(result[11]));
  xor xor_6 (xor_6_out, sub, B[10]);
  xor xor_7 (xor_7_out, sub, B[11]);
  BitAdder bitadder_6 (.A(xor_8_out), .B(A[9]), .Cin(bitadder_8_cout), .Cout(bitadder_6_cout), .Sum(result[9]));
  BitAdder bitadder_7 (.A(xor_6_out), .B(A[10]), .Cin(bitadder_6_cout), .Cout(bitadder_7_cout), .Sum(result[10]));
  xor xor_8 (xor_8_out, sub, B[9]);
  BitAdder bitadder_8 (.A(xor_9_out), .B(A[8]), .Cin(bitadder_9_cout), .Cout(bitadder_8_cout), .Sum(result[8]));
  xor xor_9 (xor_9_out, sub, B[8]);
  BitAdder bitadder_9 (.A(xor_10_out), .B(A[7]), .Cin(bitadder_10_cout), .Cout(bitadder_9_cout), .Sum(result[7]));
  xor xor_10 (xor_10_out, sub, B[7]);
  BitAdder bitadder_10 (.A(xor_11_out), .B(A[6]), .Cin(bitadder_11_cout), .Cout(bitadder_10_cout), .Sum(result[6]));
  xor xor_11 (xor_11_out, sub, B[6]);
  BitAdder bitadder_11 (.A(xor_12_out), .B(A[5]), .Cin(bitadder_12_cout), .Cout(bitadder_11_cout), .Sum(result[5]));
  xor xor_12 (xor_12_out, sub, B[5]);
  BitAdder bitadder_12 (.A(xor_13_out), .B(A[4]), .Cin(bitadder_13_cout), .Cout(bitadder_12_cout), .Sum(result[4]));
  xor xor_13 (xor_13_out, sub, B[4]);
  BitAdder bitadder_13 (.A(xor_15_out), .B(A[3]), .Cin(bitadder_14_cout), .Cout(bitadder_13_cout), .Sum(result[3]));
  xor xor_14 (xor_14_out, sub, B[2]);
  xor xor_15 (xor_15_out, sub, B[3]);
  BitAdder bitadder_14 (.A(xor_14_out), .B(A[2]), .Cin(bitadder_15_cout), .Cout(bitadder_14_cout), .Sum(result[2]));
  BitAdder bitadder_15 (.A(xor_16_out), .B(A[1]), .Cin(bitadder_16_cout), .Cout(bitadder_15_cout), .Sum(result[1]));
  xor xor_16 (xor_16_out, sub, B[1]);
  BitAdder bitadder_16 (.A(xor_17_out), .B(A[0]), .Cin(sub), .Cout(bitadder_16_cout), .Sum(result[0]));
  xor xor_17 (xor_17_out, sub, B[0]);

  // Other names for the same wires on the sheet: a00 = A[0]; a01 = A[1]; a02 = A[2]; a03 = A[3]; a04 = A[4];
  //   a05 = A[5]; a06 = A[6]; a07 = A[7]; a08 = A[8]; a09 = A[9]; b00 = B[0]; b01 = B[1]; b02 = B[2]; b03 = B[3];
  //   b04 = B[4]; b05 = B[5]; b06 = B[6]; b07 = B[7]; b08 = B[8]; b09 = B[9]
endmodule

module BitAdder (
  input  A,
  input  B,
  input  Cin,
  output Cout,
  output Sum
);

  wire and_1_out, and_2_out, xor_1_out;

  and and_1 (and_1_out, A, B);
  xor xor_1 (xor_1_out, A, B);
  and and_2 (and_2_out, xor_1_out, Cin);
  or or_1 (Cout, and_1_out, and_2_out);
  xor xor_2 (Sum, xor_1_out, Cin);
endmodule
