// Logisim project fsm.circ as structural Verilog: 1 circuit, main circuit main
module main (
  input  in2,
  input  in1,
  output out
);

  wire and_1_out, and_2_out, and_3_out, and_4_out, clock_1_out, diff, not_2_out, not_3_out, nQD1, nQD2,
       or_1_out, or_2_out, QD1, QD2, same;

  xor xor_1 (diff, in2, in1);
  and and_1 (and_1_out, nQD1, QD2);
  and and_2 (and_2_out, nQD1, nQD2);
  not not_1 (same, diff);
  or or_1 (or_1_out, same, and_1_out, and_2_out);
  not not_2 (not_2_out, or_1_out);
  Clock clock_1 (.out(clock_1_out));
  D_Flip_Flop D1 (.D(not_2_out), .Q(QD1), .Qn(nQD1), .en(clock_1_out));  // open: clk, preset, reset
  and and_3 (and_3_out, nQD2, QD1);
  and and_4 (and_4_out, nQD2, nQD1);
  or or_2 (or_2_out, diff, and_3_out, and_4_out);
  not not_3 (not_3_out, or_2_out);
  and and_5 (out, QD1, QD2);
  D_Flip_Flop D2 (.D(not_3_out), .Q(QD2), .Qn(nQD2), .en(clock_1_out));  // open: clk, preset, reset
endmodule
